# Fritzing sketch MKR1500 IoT 5G (saved by Fritzing 0.9.5d)
breadboards: 1

parts:
  Componente1 = Arduino MKR NB 1500
  LED1 = smd LED [color="Red (633nm)" package="0603 [SMD]"]  # not connected
  LED2 = smd LED [color="Yellow (595nm)" package="0603 [SMD]"]  # not connected
  S1 = Pushbutton [package="[SMD]"]
  R1 = Photocell (LDR) [package=THT]  # not connected

nets:
  N1: Componente1.RESET, Componente1.D14/TX
  N2: Componente1.D11/MOSI, Componente1.+5V
  N3: S1.Pin_1, S1.Pin_2
  N4: S1.Pin_3, S1.Pin_4

custom parts:
  Arduino MKR NB 1500: Add Narrowband communication to your project with the MKR NB 1500. It's the perfect choice for devices in remote locations without an Internet connection, or in situations in which power isn't available like on-field deployments, remote metering systems, solar-powered devices, or other extreme scenarios. The board's main processor is a low power Arm® Cortex®-M0 32-bit SAMD21, like in the other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
